# Fritzing sketch esp32 (saved by Fritzing 0.9.3b)
circuit board: 8.46667cm x 5.64444cm

parts:
  Part1 = Adafruit HUZZAH32 ESP32 Feather [part_number="Adafruit #3405"]
  hc-sr1 = hc-sr04

nets:
  N1: Part1.SCK, hc-sr1.Trig
  N2: Part1.A5_IO4, hc-sr1.Echo
  GND: Part1.GND, hc-sr1.GND
  N3: Part1.VBUS, hc-sr1.VCC
