# Fritzing sketch esp8266 (saved by Fritzing 0.9.3b)
circuit board: 8.46667cm x 5.64444cm

parts:
  WeMos_D1_Mini1 = WeMos D1 Mini
  hc-sr1 = hc-sr04

nets:
  5V: WeMos_D1_Mini1.5V, hc-sr1.VCC
  N1: WeMos_D1_Mini1.D1, hc-sr1.Trig
  N2: WeMos_D1_Mini1.D2, hc-sr1.Echo
  N3: WeMos_D1_Mini1.G, hc-sr1.GND
