# Fritzing sketch wipy (saved by Fritzing 0.9.3b)

parts:
  Part1 = WIPY 2.0/3.0 [part_number="wipy 3.0"]
  hc-sr1 = hc-sr04

nets:
  VIN: Part1.VIN, hc-sr1.VCC
  GND: Part1.GND, hc-sr1.GND
  N1: Part1.P23, hc-sr1.Trig
  N2: Part1.P22, hc-sr1.Echo
